# Fritzing sketch LoRaGateway (saved by Fritzing 0.9.0b)
perfboards: 1

parts:
  Raspberry_Pi_B_rev1 = Raspberry Pi B rev2
  20 = female pin header, 2 pins [form="♀ (female)"]  # not connected
  J3 = female pin header, 2 pins [form="♀ (female)"]
  J4 = female pin header, 2 pins [form="♀ (female)"]
  J5 = female pin header, 2 pins [form="♀ (female)"]
  J6 = female pin header, 2 pins [form="♀ (female)"]  # not connected
  J7 = female pin header, 2 pins [form="♀ (female)"]  # not connected
  J8 = female pin header, 2 pins [form="♀ (female)"]  # not connected
  J9 = female pin header, 2 pins [form="♀ (female)"]  # not connected
  J10 = female pin header, 2 pins [form="♀ (female)"]  # not connected
  1 = female pin header, 2 pins [form="♀ (female)"]  # not connected
  21 = female pin header, 2 pins [form="♀ (female)"]
  23 = female pin header, 2 pins [form="♀ (female)"]  # not connected
  J14 = female pin header, 2 pins [form="♀ (female)"]  # not connected
  J15 = female pin header, 2 pins [form="♀ (female)"]  # not connected

nets:
  N1: Raspberry_Pi_B_rev1.5V, 21.pin2
  N2: Raspberry_Pi_B_rev1.GND, 21.pin1
  N3: Raspberry_Pi_B_rev1.GPIO_10, J4.pin1
  N4: Raspberry_Pi_B_rev1.GPIO_9, J4.pin2
  N5: Raspberry_Pi_B_rev1.GPIO_25, J5.pin2
  N6: Raspberry_Pi_B_rev1.GPIO_11, J5.pin1
  N7: Raspberry_Pi_B_rev1.GPIO_8, J3.pin2
