# Fritzing sketch 02_SteuerungSchalter (saved by Fritzing 0.9.0b)
breadboards: 1

parts:
  S1 = Pushbutton [package="[THT]"]
  Raspberry_Pi_B_rev1 = Raspberry Pi B rev2
  R1 = Resistor [tolerance=±5% resistance=10k package=THT]

nets:
  N1: S1.Pin_1, S1.Pin_2, Raspberry_Pi_B_rev1.3V3
  N2: S1.Pin_3, S1.Pin_4, Raspberry_Pi_B_rev1.GPIO_23, R1.Pin_1
  N3: Raspberry_Pi_B_rev1.GND, R1.Pin_0
