# Fritzing sketch 04_Ultraschallsensor (saved by Fritzing 0.9.0b)
breadboards: 1

parts:
  Raspberry_Pi_B_rev1 = Raspberry Pi B rev2
  S1 = Ultrasound HC-SR04 [package="[THT]"]
  R1 = Resistor [tolerance=±5% resistance=220 package=THT]
  R2 = Resistor [tolerance=±5% resistance=220 package=THT]
  R3 = Resistor [tolerance=±5% resistance=1k package=THT]

nets:
  5V: Raspberry_Pi_B_rev1.5V, S1.VCC, S1.Trig
  N1: Raspberry_Pi_B_rev1.GPIO_3, S1.Echo, S1.GND, R1.Pin_1, R3.Pin_1
  N2: Raspberry_Pi_B_rev1.GPIO_24, R2.Pin_0, R3.Pin_0
  N3: R1.Pin_0, R2.Pin_1

custom parts:
  Ultrasound HC-SR04: A generic ultra sound emitter.
