# Fritzing sketch 05_Fsr (saved by Fritzing 0.9.0b)
breadboards: 1

parts:
  Raspberry_Pi_B_rev1 = Raspberry Pi B rev2
  J1 = Basic Force Sensing Resistor (FSR) [package=THT]
  R1 = Resistor [tolerance=±5% resistance=220 package=THT]

nets:
  N1: Raspberry_Pi_B_rev1.GPIO_25, J1.pin_0, R1.Pin_0
  N2: Raspberry_Pi_B_rev1.GND, R1.Pin_1
  N3: Raspberry_Pi_B_rev1.3V3, J1.pin_1
